// Logisim project ALU_C2_Group_6_LogisimEvolution.circ as structural Verilog: 2 circuits, main circuit ALU
module ALU (
  input  A4,
  input  A3,
  input  A2,
  input  A1,
  input  B4,
  input  B3,
  input  B2,
  input  B1,
  input  CS2,
  input  CS1,
  input  CS0,
  output C,
  output S,
  output V,
  output Z,
  output F4,
  output F3,
  output F2,
  output F1
);

  wire n7404_1_pin10, n7408_1_pin6, n7432_1_pin3, n7432_1_pin6, n7432_1_pin8, n7432_1_pin11, n7432_2_pin3,
       n7432_2_pin6, n7432_2_pin8, n7486_2_pin2, n7486_2_pin3, n7486_2_pin6, n7486_2_pin12, n74157_1_pin3,
       n74157_1_pin4, n74157_1_pin6, n74157_1_pin7, n74157_1_pin9, n74157_1_pin10, n74157_1_pin12,
       n74157_1_pin13, n74157_1_pin15, n74157_2_pin3, n74157_2_pin6, n74157_2_pin10, n74157_2_pin13,
       n74157_3_pin3, n74157_3_pin6, n74157_3_pin10, n74157_3_pin13, n74283_1_pin2, n74283_1_pin6,
       n74283_1_pin7, n74283_1_pin9, n74283_1_pin11, n74283_1_pin15;

  _7432 u_7432_1 (
    .pin1(A1), .pin2(B1), .pin3(n7432_1_pin3), .pin4(A2), .pin5(B2), .pin6(n7432_1_pin6), .pin13(A4),
    .pin12(B4), .pin11(n7432_1_pin11), .pin10(A3), .pin9(B3), .pin8(n7432_1_pin8));
  _74157 u_74157_1 (
    .pin1(CS0), .pin2(n7432_1_pin3), .pin3(n74157_1_pin3), .pin4(n74157_1_pin4), .pin5(n7432_1_pin6),
    .pin6(n74157_1_pin6), .pin7(n74157_1_pin7), .pin15(n74157_1_pin15), .pin14(n7432_1_pin11),
    .pin13(n74157_1_pin13), .pin12(n74157_1_pin12), .pin11(n7432_1_pin8), .pin10(n74157_1_pin10),
    .pin9(n74157_1_pin9));
  _7486 u_7486_1 (
    .pin1(A1), .pin2(B1), .pin3(n74157_1_pin3), .pin4(A2), .pin5(B2), .pin6(n74157_1_pin6), .pin13(A4),
    .pin12(B4), .pin11(n74157_1_pin13), .pin10(A3), .pin9(B3), .pin8(n74157_1_pin10));
  _74157 u_74157_2 (
    .pin1(CS1), .pin2(n74157_1_pin4), .pin3(n74157_2_pin3), .pin4(F1), .pin5(n74157_1_pin7),
    .pin6(n74157_2_pin6), .pin7(F2), .pin15(n74157_1_pin15), .pin14(n74157_1_pin12), .pin13(n74157_2_pin13),
    .pin12(F4), .pin11(n74157_1_pin9), .pin10(n74157_2_pin10), .pin9(F3));
  _7432 u_7432_2 (
    .pin1(F1), .pin2(F2), .pin3(n7432_2_pin3), .pin4(n7432_2_pin3), .pin5(F3), .pin6(n7432_2_pin6),
    .pin10(F4), .pin9(n7432_2_pin6), .pin8(n7432_2_pin8));  // open: pin13, pin12, pin11
  _74283 u_74283_1 (
    .pin1(n74157_2_pin6), .pin2(n74283_1_pin2), .pin3(A2), .pin4(n74157_2_pin3), .pin5(A1),
    .pin6(n74283_1_pin6), .pin7(n74283_1_pin7), .pin15(n74283_1_pin15), .pin14(A3), .pin13(n74157_2_pin10),
    .pin12(A4), .pin11(n74283_1_pin11), .pin10(n74157_2_pin13), .pin9(n74283_1_pin9));
  _74157 u_74157_3 (
    .pin1(CS2), .pin2(B1), .pin3(n74157_3_pin3), .pin4(n74283_1_pin6), .pin5(B2), .pin6(n74157_3_pin6),
    .pin7(n74283_1_pin2), .pin15(CS0), .pin14(B4), .pin13(n74157_3_pin13), .pin12(n74283_1_pin11),
    .pin11(B3), .pin10(n74157_3_pin10), .pin9(n74283_1_pin15));
  _7486 u_7486_2 (
    .pin1(A4), .pin2(n7486_2_pin2), .pin3(n7486_2_pin3), .pin4(A4), .pin5(n74157_2_pin13),
    .pin6(n7486_2_pin6), .pin13(n7432_2_pin8), .pin12(n7486_2_pin12), .pin11(Z));  // open: pin10, pin9, pin8
  _7404 u_7404_1 (
    .pin1(B1), .pin2(n74157_3_pin3), .pin3(B2), .pin4(n74157_3_pin6), .pin5(B3), .pin6(n74157_3_pin10),
    .pin13(n74283_1_pin11), .pin12(n7486_2_pin2), .pin11(CS2), .pin10(n7404_1_pin10), .pin9(B4),
    .pin8(n74157_3_pin13));
  _7408 u_7408_1 (
    .pin1(n74283_1_pin9), .pin2(CS1), .pin3(C), .pin4(n7486_2_pin3), .pin5(n7486_2_pin6),
    .pin6(n7408_1_pin6), .pin13(CS0), .pin12(n7404_1_pin10), .pin11(n74283_1_pin7), .pin10(n7408_1_pin6),
    .pin9(CS1), .pin8(V));

  assign S = F4;
  // also tied to GND on the sheet: n74157_1_pin15
  // also tied to VCC on the sheet: n7486_2_pin12

  // Notes on the sheet:
  //   Strobe
endmodule

module ALUTester (
  input  [3:0] A,
  input  [3:0] B,
  input  [2:0] Controls,
  output [3:0] Flags,
  output [3:0] F
);

  ALU alu_1 (
    .A4(A[3]), .A3(A[2]), .A2(A[1]), .A1(A[0]), .B4(B[3]), .B3(B[2]), .B2(B[1]), .B1(B[0]),
    .CS2(Controls[2]), .CS1(Controls[1]), .CS0(Controls[0]), .C(Flags[3]), .S(Flags[2]), .V(Flags[1]),
    .Z(Flags[0]), .F4(F[3]), .F3(F[2]), .F2(F[1]), .F1(F[0]));

  // Notes on the sheet:
  //   CSVZ
endmodule
