// Logisim project FPA_C2_Group6_Logisim_Evolution.circ as structural Verilog
module main (
  input  [15:0] A,
  input  [15:0] B,
  output [15:0] Result
);

  wire Comp_and_align_final_sign, Comp_and_align_smaller_sign;
  wire [3:0] Comp_and_align_common_exponent, Normalizer_1_exponent_normalized;
  wire [13:0] Comp_and_align_greater_mantissa_14, Comp_and_align_smaller_mantissa_14;
  wire [14:0] Arithmetic_op_result_15, Normalizer_1_result_normalized, Normalizer_2_result_normalized,
       Rounder_rounded_mantissa;

  Comparison_and_alignment Comp_and_align (
    .A_sign(A[15]), .B_sign(B[15]), .A_exponent(A[14:11]), .B_exponent(B[14:11]), .A_mantissa(A[10:0]),
    .B_mantissa(B[10:0]), .Final_sign(Comp_and_align_final_sign), .Smaller_sign(Comp_and_align_smaller_sign),
    .Common_exponent(Comp_and_align_common_exponent),
    .Greater_mantissa_14(Comp_and_align_greater_mantissa_14),
    .Smaller_mantissa_14(Comp_and_align_smaller_mantissa_14));
  Arithmetic Arithmetic_op (
    .Greater_sign(Comp_and_align_final_sign), .Smaller_sign(Comp_and_align_smaller_sign),
    .Greater_mantissa_14(Comp_and_align_greater_mantissa_14),
    .Smaller_mantissa_14(Comp_and_align_smaller_mantissa_14), .Final_sign(Result[15]),
    .Result_15(Arithmetic_op_result_15));
  Normalization_15 Normalizer_1 (
    .Common_exponent(Comp_and_align_common_exponent), .Resultant_mantissa(Arithmetic_op_result_15),
    .Exponent_normalized(Normalizer_1_exponent_normalized), .Result_normalized(Normalizer_1_result_normalized));
  Rounding Rounder (.Resultant_mantissa(Normalizer_1_result_normalized), .Rounded_mantissa(Rounder_rounded_mantissa));
  Normalization_15 Normalizer_2 (
    .Common_exponent(Normalizer_1_exponent_normalized), .Resultant_mantissa(Rounder_rounded_mantissa),
    .Exponent_normalized(Result[14:11]),
    .Result_normalized({Normalizer_2_result_normalized[14:13], Result[10:0], Normalizer_2_result_normalized[1:0]}));
endmodule

module Comparison_and_alignment (
  input  A_sign,
  input  B_sign,
  input  [3:0] A_exponent,
  input  [3:0] B_exponent,
  input  [10:0] A_mantissa,
  input  [10:0] B_mantissa,
  output Final_sign,
  output Smaller_sign,
  output [3:0] Common_exponent,
  output [13:0] Greater_mantissa_14,
  output [13:0] Smaller_mantissa_14
);

  wire and_1_out, comparator_1_eq, comparator_1_gt, comparator_2_eq, comparator_2_gt, or_1_out, Select_out,
       subtractor_1_bout;
  wire [3:0] MUX_17_smaller_exponent, subtractor_1_out;
  wire [11:0] MUX_17_smaller_mantissa_12;

  Comparator #(.mode("unsigned"), .width(4)) comparator_1 (
    .a(A_exponent), .b(B_exponent), .gt(comparator_1_gt), .eq(comparator_1_eq));  // open: lt
  Comparator #(.mode("unsigned"), .width(12)) comparator_2 (
    .a({1'b1, A_mantissa}), .b({1'b1, B_mantissa}), .gt(comparator_2_gt), .eq(comparator_2_eq));  // open: lt
  and and_1 (and_1_out, comparator_1_eq, or_1_out);
  or or_1 (or_1_out, comparator_2_gt, comparator_2_eq);
  or Select (Select_out, and_1_out, comparator_1_gt);
  MUX_17bit MUX_17 (
    .A_sign(A_sign), .B_sign(B_sign), .A_exponent(A_exponent), .B_exponent(B_exponent),
    .A_mantissa({1'b1, A_mantissa}), .B_mantissa({1'b1, B_mantissa}), .Select(Select_out),
    .Final_sign(Final_sign), .Smaller_sign(Smaller_sign), .Common_exponent(Common_exponent),
    .Smaller_exponent(MUX_17_smaller_exponent), .Greater_mantissa_12(Greater_mantissa_14[13:2]),
    .Smaller_mantissa_12(MUX_17_smaller_mantissa_12));
  Subtractor #(.width(4)) subtractor_1 (
    .a(Common_exponent), .b(MUX_17_smaller_exponent), .out(subtractor_1_out), .bin(1'b0),
    .bout(subtractor_1_bout));
  // Probe on subtractor_1_bout
  Shifter #(.shift("lr"), .width(14)) shifter_1 (
    .in({MUX_17_smaller_mantissa_12, 2'b00}), .\dist (subtractor_1_out), .out(Smaller_mantissa_14));

  assign Greater_mantissa_14[1:0] = 2'b00;

  // Notes on the sheet:
  //   Select = (A_exp > B_exp) OR ((A_exp = B_exp) AND (A_mant >= B_mant))
  //   Checks if A>=B, else flips to keep greater number at top
  //   Does necessary shifting on the smaller number to ensure they're aligned
endmodule

module MUX_17bit (
  input  A_sign,
  input  B_sign,
  input  [3:0] A_exponent,
  input  [3:0] B_exponent,
  input  [11:0] A_mantissa,
  input  [11:0] B_mantissa,
  input  Select,
  output Final_sign,
  output Smaller_sign,
  output [3:0] Common_exponent,
  output [3:0] Smaller_exponent,
  output [11:0] Greater_mantissa_12,
  output [11:0] Smaller_mantissa_12
);

  wire not_1_out, or_1_out, or_2_out;

  not not_1 (not_1_out, Select);
  Multiplexer multiplexer_1 (.in0(A_sign), .in1(B_sign), .out(Final_sign), .sel(not_1_out));
  Multiplexer multiplexer_2 (.in0(A_sign), .in1(B_sign), .out(Smaller_sign), .sel(Select));
  Multiplexer #(.width(4)) multiplexer_3 (.in0(A_exponent), .in1(B_exponent), .out(Common_exponent), .sel(not_1_out));
  Multiplexer #(.width(4)) multiplexer_4 (.in0(A_exponent), .in1(B_exponent), .out(Smaller_exponent), .sel(Select));
  Multiplexer #(.enable("true"), .width(12)) multiplexer_5 (
    .in0(A_mantissa), .in1(B_mantissa), .out(Greater_mantissa_12), .sel(not_1_out), .en(or_1_out));
  Multiplexer #(.enable("true"), .width(12)) multiplexer_6 (
    .in0(A_mantissa), .in1(B_mantissa), .out(Smaller_mantissa_12), .sel(Select), .en(or_2_out));
  or or_1 (or_1_out, Common_exponent[0], Common_exponent[1], Common_exponent[3], Common_exponent[2]);
  or or_2 (or_2_out, Smaller_exponent[0], Smaller_exponent[1], Smaller_exponent[3], Smaller_exponent[2]);

  // Notes on the sheet:
  //   Swapps if A < B
endmodule

module Arithmetic (
  input  Greater_sign,
  input  Smaller_sign,
  input  [13:0] Greater_mantissa_14,
  input  [13:0] Smaller_mantissa_14,
  output Final_sign,
  output [14:0] Result_15
);

  wire adder_1_cout, not_1_out, subtractor_1_bout, xor_1_out;
  wire [13:0] adder_1_out, subtractor_1_out;

  xor xor_1 (xor_1_out, Greater_sign, Smaller_sign);
  Adder #(.width(14)) adder_1 (
    .a(Greater_mantissa_14), .b(Smaller_mantissa_14), .out(adder_1_out), .cin(1'b0), .cout(adder_1_cout));
  Subtractor #(.width(14)) subtractor_1 (
    .a(Greater_mantissa_14), .b(Smaller_mantissa_14), .out(subtractor_1_out), .bin(1'b0),
    .bout(subtractor_1_bout));
  // Probe on subtractor_1_bout
  not not_1 (not_1_out, xor_1_out);
  and and_1 (Result_15[14], not_1_out, adder_1_cout);
  Multiplexer #(.width(14)) multiplexer_1 (
    .in0(adder_1_out), .in1(subtractor_1_out), .out(Result_15[13:0]), .sel(xor_1_out));

  assign Final_sign = Greater_sign;

  // Notes on the sheet:
  //   Selects between addition and subtraction, also sets the final sign
  //   Carry (for addition)
endmodule

module Normalization_15 (
  input  [3:0] Common_exponent,
  input  [14:0] Resultant_mantissa,
  output [3:0] Exponent_normalized,
  output [14:0] Result_normalized
);

  wire adder_1_cout, and_1_out, and_2_out, comparator_1_eq, comparator_1_lt, Inv_exp_detector_2_all_0s,
       Inv_exp_detector_2_all_1s, Inv_exp_detector_all_0s, Inv_exp_detector_all_1s, not_1_out, not_2_out,
       not_3_out, or_1_out, or_2_out, or_3_out, Priority_encoder_fifteen_is_zero,
       Priority_encoder_fifteen_last_bit, subtractor_1_bout, subtractor_2_bout;
  wire [3:0] adder_1_out, multiplexer_1_out, Priority_encoder_fifteen_leading_1_position, subtractor_1_out,
       subtractor_2_out;
  wire [14:0] multiplexer_2_out, shifter_1_out, shifter_2_out;

  Priority_encoder_15 Priority_encoder_fifteen (
    .Resultant_mantissa(Resultant_mantissa),
    .Leading_1_position(Priority_encoder_fifteen_leading_1_position),
    .Last_bit(Priority_encoder_fifteen_last_bit), .Is_zero(Priority_encoder_fifteen_is_zero));
  Subtractor #(.width(4)) subtractor_1 (
    .a(4'b1101), .b(Priority_encoder_fifteen_leading_1_position), .out(subtractor_1_out), .bin(1'b0),
    .bout(subtractor_1_bout));
  // Probe on subtractor_1_bout
  Comparator #(.mode("unsigned"), .width(4)) comparator_1 (
    .a(Common_exponent), .b(subtractor_1_out), .eq(comparator_1_eq), .lt(comparator_1_lt));  // open: gt
  Subtractor #(.width(4)) subtractor_2 (
    .a(Common_exponent), .b(subtractor_1_out), .out(subtractor_2_out), .bin(1'b0), .bout(subtractor_2_bout));
  // Probe on subtractor_2_bout
  Adder #(.width(4)) adder_1 (.a(Common_exponent), .b(4'b0001), .out(adder_1_out), .cin(1'b0), .cout(adder_1_cout));
  // Probe on adder_1_cout
  or or_1 (or_1_out, comparator_1_eq, comparator_1_lt);
  not not_1 (not_1_out, Priority_encoder_fifteen_last_bit);
  Shifter #(.width(15)) shifter_1 (.in(Resultant_mantissa), .\dist (subtractor_1_out), .out(shifter_1_out));
  Shifter #(.shift("lr"), .width(15)) shifter_2 (.in(Resultant_mantissa), .\dist (4'b0001), .out(shifter_2_out));
  and and_1 (and_1_out, or_1_out, not_1_out);
  Multiplexer #(.width(4)) multiplexer_1 (
    .in0(subtractor_2_out), .in1(adder_1_out), .out(multiplexer_1_out),
    .sel(Priority_encoder_fifteen_last_bit));
  Multiplexer #(.width(15)) multiplexer_2 (
    .in0(shifter_1_out), .in1(shifter_2_out), .out(multiplexer_2_out), .sel(Priority_encoder_fifteen_last_bit));
  Inv_exponent_detector_4 Inv_exp_detector (
    .Exponent(Common_exponent), .All_0s(Inv_exp_detector_all_0s), .All_1s(Inv_exp_detector_all_1s));
  not not_2 (not_2_out, or_2_out);
  or or_2 (or_2_out, Inv_exp_detector_all_0s, and_1_out, and_2_out);
  and and_2 (and_2_out, Priority_encoder_fifteen_is_zero, not_3_out);
  not not_3 (not_3_out, Inv_exp_detector_all_1s);
  Multiplexer #(.enable("true"), .width(4)) multiplexer_3 (
    .in0(multiplexer_1_out), .in1(4'b1111), .out(Exponent_normalized), .sel(Inv_exp_detector_all_1s),
    .en(not_2_out));
  Inv_exponent_detector_4 Inv_exp_detector_2 (
    .Exponent(Exponent_normalized), .All_0s(Inv_exp_detector_2_all_0s), .All_1s(Inv_exp_detector_2_all_1s));
  Multiplexer #(.width(15)) multiplexer_4 (
    .in0(multiplexer_2_out), .in1(15'h2000), .out(Result_normalized), .sel(or_3_out));
  or or_3 (or_3_out, Inv_exp_detector_2_all_0s, Inv_exp_detector_2_all_1s);

  // Notes on the sheet:
  //   Normalizes input. Also ensures that zero mantissa gets translated to zero exponent and all 1's exponent stays all 1's, all 0's stay 0's
  //   Makes exponent zero if mantissa is zero
  //   Has two main modes: shift right mode (when there's a carry out from adder) and shift left mode (which covers no shift case along with smaller mantissa case)
  //   To ensure exponent doesn't go from 1111 to 0000 or other numbers and from 0000 to another number
  //   Also to ensure that invalid exponents don't get generated when shifting left by large number of bits
  //   Set to 1 (actual mantissa/fraction set to zero) when all exp is 0s or 1s to cause no new issues being introduced in rounding
endmodule

module Priority_encoder_15 (
  input  [14:0] Resultant_mantissa,
  output [3:0] Leading_1_position,
  output Last_bit,
  output Is_zero
);

  wire priority_encoder_1_en_out, priority_encoder_1_gs;
  wire [3:0] priority_encoder_1_out;

  // Probe on priority_encoder_1_en_out
  Priority_Encoder #(.select(4)) priority_encoder_1 (
    .in0(Resultant_mantissa[0]), .in1(Resultant_mantissa[1]), .in2(Resultant_mantissa[2]),
    .in3(Resultant_mantissa[3]), .in4(Resultant_mantissa[4]), .in5(Resultant_mantissa[5]),
    .in6(Resultant_mantissa[6]), .in7(Resultant_mantissa[7]), .in8(Resultant_mantissa[8]),
    .in9(Resultant_mantissa[9]), .in10(Resultant_mantissa[10]), .in11(Resultant_mantissa[11]),
    .in12(Resultant_mantissa[12]), .in13(Resultant_mantissa[13]), .in14(Resultant_mantissa[14]), .in15(1'b0),
    .out(priority_encoder_1_out), .gs(priority_encoder_1_gs), .en_out(priority_encoder_1_en_out), .en_in(1'b1));
  Multiplexer #(.width(4)) multiplexer_1 (
    .in0(4'b1101), .in1(priority_encoder_1_out), .out(Leading_1_position), .sel(priority_encoder_1_gs));
  not not_1 (Is_zero, priority_encoder_1_gs);

  assign Last_bit = Resultant_mantissa[14];

  // Notes on the sheet:
  //   Finds the location of the leading 1. Also checks if the input is not all zeros (for handling zero result case)
  //   Last bit extracted here is for selecting between the two cases of normalization
endmodule

module Inv_exponent_detector_4 (
  input  [3:0] Exponent,
  output All_0s,
  output All_1s
);

  nor nor_1 (All_0s, Exponent[0], Exponent[1], Exponent[3], Exponent[2]);
  and and_1 (All_1s, Exponent[0], Exponent[1], Exponent[3], Exponent[2]);
endmodule

module Rounding (
  input  [14:0] Resultant_mantissa,
  output [14:0] Rounded_mantissa
);

  Adder #(.width(13)) adder_1 (
    .a(Resultant_mantissa[14:2]), .b({{12{1'b0}}, Resultant_mantissa[1]}), .out(Rounded_mantissa[14:2]),
    .cin(1'b0));  // open: cout

  assign Rounded_mantissa[1:0] = 2'b00;
endmodule
