// Logisim project MIPS_C2_G6_HSC22.circ as structural Verilog: 6 circuits, main circuit main
module main (
  output [3:0] t0,
  output [3:0] t1,
  output [3:0] t2,
  output [3:0] t3,
  output [3:0] t4,
  output [3:0] sp
);

  wire ALU_part_zero, Clk_out, Control_part_alusrc, Control_part_branch, Control_part_branchtype,
       Control_part_jump, Control_part_memread, Control_part_memtoreg, Control_part_memwrite,
       Control_part_regdst, Control_part_regwrite, Reset_out, TakeBranch_out, xor_1_out;
  wire [2:0] Control_part_aluop;
  wire [3:0] ALU_part_result, Data_Mem_dataread, Instruction_PC_dreg_sft_adr_imdt, Instruction_PC_opcode,
       Instruction_PC_sreg1, Instruction_PC_sreg2_dreg, multiplexer_1_out, multiplexer_2_out,
       multiplexer_5_out, Registers_part_readdata1, Registers_part_readdata2;
  wire [7:0] adder_1_out, adder_2_out, bit_extender_1_out, Instruction_PC_jumpadr, Instruction_PC_pcread,
       multiplexer_3_out, multiplexer_4_out;

  // Probe on multiplexer_4_out
  Clock Clk (.out(Clk_out));
  Button Reset (.out(Reset_out));
  Adder adder_1 (.a(8'h1), .b(Instruction_PC_pcread), .out(adder_1_out), .cin(1'b0));  // open: cout
  // Probe on Instruction_PC_pcread
  // Probe on Instruction_PC_opcode
  InstructionMem Instruction_PC (
    .PCWrite(multiplexer_4_out), .Clock(Clk_out), .Reset(Reset_out), .PCRead(Instruction_PC_pcread),
    .JumpAdr(Instruction_PC_jumpadr), .OpCode(Instruction_PC_opcode), .SReg1(Instruction_PC_sreg1),
    .SReg2_DReg(Instruction_PC_sreg2_dreg), .DReg_Sft_Adr_Imdt(Instruction_PC_dreg_sft_adr_imdt));
  // Probe on Instruction_PC_dreg_sft_adr_imdt
  assign bit_extender_1_out = {{4{Instruction_PC_dreg_sft_adr_imdt[3]}}, Instruction_PC_dreg_sft_adr_imdt};  // Bit_Extender bit_extender_1
  // Probe on Instruction_PC_sreg1
  // Probe on Instruction_PC_sreg2_dreg
  Multiplexer #(.width(4)) multiplexer_1 (
    .in0(Instruction_PC_sreg2_dreg), .in1(Instruction_PC_dreg_sft_adr_imdt), .out(multiplexer_1_out),
    .sel(Control_part_regdst));
  // Probe on multiplexer_1_out
  Adder adder_2 (.a(bit_extender_1_out), .b(adder_1_out), .out(adder_2_out), .cin(1'b0));  // open: cout
  Control Control_part (
    .OpCode(Instruction_PC_opcode), .RegDst(Control_part_regdst), .RegWrite(Control_part_regwrite),
    .Branch(Control_part_branch), .BranchType(Control_part_branchtype), .Jump(Control_part_jump),
    .MemRead(Control_part_memread), .MemToReg(Control_part_memtoreg), .MemWrite(Control_part_memwrite),
    .ALUSrc(Control_part_alusrc), .ALUOp(Control_part_aluop));
  Registers Registers_part (
    .RegWrite(Control_part_regwrite), .SrcReg1(Instruction_PC_sreg1), .SrcReg2(Instruction_PC_sreg2_dreg),
    .DstReg(multiplexer_1_out), .WriteData(multiplexer_5_out), .Clock(Clk_out), .Reset(Reset_out),
    .RegDisplay({sp, t4, t3, t2, t1, t0}), .ReadData1(Registers_part_readdata1),
    .ReadData2(Registers_part_readdata2));
  // Probe on Registers_part_readdata1
  Multiplexer #(.width(4)) multiplexer_2 (
    .in0(Registers_part_readdata2), .in1(Instruction_PC_dreg_sft_adr_imdt), .out(multiplexer_2_out),
    .sel(Control_part_alusrc));
  // Probe on multiplexer_2_out
  // Probe on Instruction_PC_dreg_sft_adr_imdt
  Multiplexer #(.width(8)) multiplexer_3 (
    .in0(adder_1_out), .in1(adder_2_out), .out(multiplexer_3_out), .sel(TakeBranch_out));
  and TakeBranch (TakeBranch_out, Control_part_branch, xor_1_out);
  xor xor_1 (xor_1_out, Control_part_branchtype, ALU_part_zero);
  // Probe on Control_part_aluop
  Multiplexer #(.width(8)) multiplexer_4 (
    .in0(multiplexer_3_out), .in1(Instruction_PC_jumpadr), .out(multiplexer_4_out), .sel(Control_part_jump));
  // Probe on Registers_part_readdata2
  // Probe on multiplexer_5_out
  ALU ALU_part (
    .ALUOp(Control_part_aluop), .A(Registers_part_readdata1), .B(multiplexer_2_out), .Zero(ALU_part_zero),
    .Result(ALU_part_result));
  Hex_Digit_Display t_0 (.value(t0));  // open: dp
  Hex_Digit_Display t_3 (.value(t3));  // open: dp
  // Probe on ALU_part_result
  Hex_Digit_Display t_1 (.value(t1));  // open: dp
  Hex_Digit_Display t_4 (.value(t4));  // open: dp
  Hex_Digit_Display t_2 (.value(t2));  // open: dp
  Hex_Digit_Display s_p (.value(sp));  // open: dp
  DataMem Data_Mem (
    .Address(ALU_part_result), .MemRead(Control_part_memread), .MemWrite(Control_part_memwrite),
    .WriteData(Registers_part_readdata2), .Clock(Clk_out), .Reset(Reset_out), .DataRead(Data_Mem_dataread));
  Multiplexer #(.width(4)) multiplexer_5 (
    .in0(ALU_part_result), .in1(Data_Mem_dataread), .out(multiplexer_5_out), .sel(Control_part_memtoreg));

  // Notes on the sheet:
  //   t0            t1            t2
  //   t3            t4            sp
endmodule

module Registers (
  input  RegWrite,
  input  [3:0] SrcReg1,
  input  [3:0] SrcReg2,
  input  [3:0] DstReg,
  input  [3:0] WriteData,
  input  Clock,
  input  Reset,
  output [23:0] RegDisplay,
  output [3:0] ReadData1,
  output [3:0] ReadData2
);

  wire demultiplexer_1_out1, demultiplexer_1_out2, demultiplexer_1_out3, demultiplexer_1_out4,
       demultiplexer_1_out5, demultiplexer_1_out7;

  Register #(.trigger("falling"), .width(4)) t1 (
    .D(WriteData), .en(demultiplexer_1_out1), .clk(Clock), .Q(RegDisplay[7:4]), .clr(Reset));
  Register #(.trigger("falling"), .width(4)) t2 (
    .D(WriteData), .en(demultiplexer_1_out2), .clk(Clock), .Q(RegDisplay[11:8]), .clr(Reset));
  Multiplexer #(.disabled("Z"), .select(3), .width(4)) multiplexer_1 (
    .in0(4'b0000), .in1(RegDisplay[7:4]), .in2(RegDisplay[11:8]), .in3(RegDisplay[15:12]),
    .in4(RegDisplay[19:16]), .in5(RegDisplay[3:0]), .in6(4'b0000), .in7(RegDisplay[23:20]), .out(ReadData1),
    .sel(SrcReg1[2:0]));
  Demultiplexer #(.disabled("Z"), .select(3)) demultiplexer_1 (
    .out1(demultiplexer_1_out1), .out2(demultiplexer_1_out2), .out3(demultiplexer_1_out3),
    .out4(demultiplexer_1_out4), .out5(demultiplexer_1_out5), .out7(demultiplexer_1_out7), .in(RegWrite),
    .sel(DstReg[2:0]));  // open: out0, out6
  Register #(.trigger("falling"), .width(4)) t3 (
    .D(WriteData), .en(demultiplexer_1_out3), .clk(Clock), .Q(RegDisplay[15:12]), .clr(Reset));
  Register #(.trigger("falling"), .width(4)) t4 (
    .D(WriteData), .en(demultiplexer_1_out4), .clk(Clock), .Q(RegDisplay[19:16]), .clr(Reset));
  Multiplexer #(.disabled("Z"), .select(3), .width(4)) multiplexer_2 (
    .in0(4'b0000), .in1(RegDisplay[7:4]), .in2(RegDisplay[11:8]), .in3(RegDisplay[15:12]),
    .in4(RegDisplay[19:16]), .in5(RegDisplay[3:0]), .in6(4'b0000), .in7(RegDisplay[23:20]), .out(ReadData2),
    .sel(SrcReg2[2:0]));
  Register #(.trigger("falling"), .width(4)) t0 (
    .D(WriteData), .en(demultiplexer_1_out5), .clk(Clock), .Q(RegDisplay[3:0]), .clr(Reset));
  Register #(.trigger("falling"), .width(4)) sp (
    .D(WriteData), .en(demultiplexer_1_out7), .clk(Clock), .Q(RegDisplay[23:20]), .clr(Reset));
endmodule

module ALU (
  input  [2:0] ALUOp,
  input  [3:0] A,
  input  [3:0] B,
  output Zero,
  output [3:0] Result
);

  wire [3:0] adder_1_out, and_1_out, nor_1_out, or_1_out, shifter_1_out, shifter_2_out, subtractor_1_out;

  Adder #(.width(4)) adder_1 (.a(A), .b(B), .out(adder_1_out), .cin(1'b0));  // open: cout
  Subtractor #(.width(4)) subtractor_1 (.a(A), .b(B), .out(subtractor_1_out), .bin(1'b0));  // open: bout
  Shifter #(.width(4)) shifter_1 (.in(A), .\dist (B[1:0]), .out(shifter_1_out));
  Shifter #(.shift("lr"), .width(4)) shifter_2 (.in(A), .\dist (B[1:0]), .out(shifter_2_out));
  assign and_1_out = A & B;  // AND_Gate and_1, 4 bits wide
  assign or_1_out = A | B;  // OR_Gate or_1, 4 bits wide
  assign nor_1_out = ~(A | B);  // NOR_Gate nor_1, 4 bits wide
  Multiplexer #(.select(3), .width(4)) multiplexer_1 (
    .in0(and_1_out), .in1(or_1_out), .in2(adder_1_out), .in3(subtractor_1_out), .in4(nor_1_out),
    .in5(shifter_1_out), .in6(shifter_2_out), .in7(4'b0000), .out(Result), .sel(ALUOp));
  nor nor_2 (Zero, Result[0], Result[1], Result[2], Result[3]);

  // Notes on the sheet:
  //   Operations: and, or, add, subtract, nor, shift left, shift right, zero
  //   0,    1,    2,        3,         4,        5,            6,           7  
endmodule

module InstructionMem (
  input  [7:0] PCWrite,
  input  Clock,
  input  Reset,
  output [7:0] PCRead,
  output [7:0] JumpAdr,
  output [3:0] OpCode,
  output [3:0] SReg1,
  output [3:0] SReg2_DReg,
  output [3:0] DReg_Sft_Adr_Imdt
);

  Register #(.trigger("falling")) PC (.D(PCWrite), .en(1'b1), .clk(Clock), .Q(PCRead), .clr(Reset));
  ROM #(.dataWidth(16)) InstructionMem (.addr(PCRead), .data({OpCode, JumpAdr, DReg_Sft_Adr_Imdt}));

  assign SReg1 = JumpAdr[7:4];
  assign SReg2_DReg = JumpAdr[3:0];

  // Notes on the sheet:
  //   contents of InstructionMem (hex, n*v repeats v):
  //   207f 2055 2013 e512 4513 8336 551 a251 9120 5034 3044 5740 1771 2771 3710 d011 7125 b154 9120
endmodule

module DataMem (
  input  [3:0] Address,
  input  MemRead,
  input  MemWrite,
  input  [3:0] WriteData,
  input  Clock,
  input  Reset,
  output [3:0] DataRead
);

  RAM #(.addrWidth(4), .asyncread("true"), .clearpin("true"), .dataWidth(4), .trigger("falling")) DataMem (
    .addr(Address), .we(MemWrite), .oe(MemRead), .clk(Clock), .din(WriteData), .dout(DataRead), .clr(Reset));
endmodule

module Control (
  input  [3:0] OpCode,
  output RegDst,
  output RegWrite,
  output Branch,
  output BranchType,
  output Jump,
  output MemRead,
  output MemToReg,
  output MemWrite,
  output ALUSrc,
  output [2:0] ALUOp
);

  ROM #(.addrWidth(4), .dataWidth(12)) Control (
    .addr(OpCode),
    .data({RegDst, RegWrite, Branch, BranchType, Jump, MemRead, MemToReg, MemWrite, ALUSrc, ALUOp}));

  // Notes on the sheet:
  //   contents of Control (hex, n*v repeats v):
  //   40e 40b 40a 46a c00 1a 40d c02 409 82 203 c04 c01 303 c03 408
  //   BranchType = 0 for beq, 1 for bne
endmodule
